// Digital circuit D-70-submission1.dig as structural Verilog
module D_70_submission1 (
  input  clk,
  input  RST,
  input  \input ,
  input  CE,
  input  SELECT,
  output \sequence 
);

  wire multiplexer_1_out, reg_rst_ce_1_p6, reg_rst_ce_2_p5, reg_rst_ce_3_p5, reg_rst_ce_4_p5,
       reg_rst_ce_5_p5, reg_rst_ce_6_p5, reg_rst_ce_7_p5, xor_1_out, xor_2_out, xor_3_out, xor_4_out,
       xor_5_out;

  Multiplexer multiplexer_1 (.sel(SELECT), .in_0(xor_1_out), .in_1(\input ), .out(multiplexer_1_out));
  // REG_RST_CE reg_rst_ce_1: pin names not known; wires that end beside it: RST, multiplexer_1_out, clk, RST, CE, reg_rst_ce_1_p6
  xor xor_1 (xor_1_out, reg_rst_ce_1_p6, xor_2_out);
  // REG_RST_CE reg_rst_ce_2: pin names not known; wires that end beside it: reg_rst_ce_1_p6, clk, RST, CE, reg_rst_ce_2_p5
  xor xor_2 (xor_2_out, reg_rst_ce_2_p5, xor_3_out);
  // REG_RST_CE reg_rst_ce_3: pin names not known; wires that end beside it: reg_rst_ce_2_p5, clk, RST, CE, reg_rst_ce_3_p5
  xor xor_3 (xor_3_out, reg_rst_ce_3_p5, xor_4_out);
  // REG_RST_CE reg_rst_ce_4: pin names not known; wires that end beside it: reg_rst_ce_3_p5, clk, RST, CE, reg_rst_ce_4_p5
  // REG_RST_CE reg_rst_ce_5: pin names not known; wires that end beside it: reg_rst_ce_4_p5, clk, RST, CE, reg_rst_ce_5_p5
  // REG_RST_CE reg_rst_ce_6: pin names not known; wires that end beside it: reg_rst_ce_5_p5, clk, RST, CE, reg_rst_ce_6_p5
  xor xor_4 (xor_4_out, reg_rst_ce_6_p5, xor_5_out);
  // REG_RST_CE reg_rst_ce_7: pin names not known; wires that end beside it: reg_rst_ce_6_p5, clk, RST, CE, reg_rst_ce_7_p5
  xor xor_5 (xor_5_out, reg_rst_ce_7_p5, \sequence );
  // REG_RST_CE reg_rst_ce_8: pin names not known; wires that end beside it: reg_rst_ce_7_p5, clk, RST, CE, \sequence 
endmodule

/* Test case experiment1:
clk input RST sequence CE SELECT
0 0  1 0 1 1
C 0  1 0 1 1
#RESET, now values are known, start init. values
C 1  0 0 1 1 #SELECT = 1 for initial values
C 0  0 0 1 1
C 0  0 0 1 1
C 0  0 0 1 1
C 0  0 0 1 1
C 0  0 0 1 1
C 0  0 0 1 1
C 0  0 1 1 1	#initial values loaded, state 0
C 0  0 0 1 0
C 0  0 0 1 0
C 0  0 0 1 0
C 0  0 0 1 0
C 0  0 0 1 0
C 0  0 0 1 0
C 0  0 0 1 0
C 0  0 1 1 0
C 0  0 1 1 0
C 0  0 0 1 0
C 0  0 0 1 0
C 0  0 1 1 0
C 0  0 1 1 0
C 0  0 1 1 0
*/

/* Test case experiment2:
clk input RST sequence CE SELECT
0 0  1 0 1 1
C 0  1 0 1 1 
#RESET, now values are known, start init. values
C 1  0 0 1 1
C 0  0 0 1 1
C 0  0 0 1 1
C 1  0 0 1 1
C 0  0 0 1 1
C 0  0 0 1 1
C 1  0 0 1 1
#start
C 0  0 1 1 1	#initial values loaded, state 0
C 0  0 0 1 0
C 0  0 0 1 0
C 0  0 1 1 0
C 0  0 0 1 0
C 0  0 0 1 0
C 0  0 1 1 0
C 0  0 0 1 0	#state 7
C 0  0 0 0 0	#start 5 idle cycles
C 0  0 0 0 0
C 0  0 0 0 0
C 0  0 0 0 0
C 0  0 0 0 0	#end idle cycles, reload
C 0  1 0 1 0
C 0  1 0 1 0
#RESET, now values are known, start init. values
C 1  0 0 1 1
C 0  0 0 1 1
C 0  0 0 1 1
C 0  0 0 1 1
C 0  0 0 1 1
C 0  0 0 1 1
C 0  0 0 1 1
C 0  0 1 1 1	#initial values loaded, state 0
C 0  0 0 1 0
C 0  0 0 1 0
C 0  0 0 1 0
C 0  0 0 1 0
*/
